# Fritzing sketch Garage Door Opener Bluetooth (saved by Fritzing 0.9.4)
circuit board: 8.46667cm x 5.64444cm
breadboards: 1

parts:
  Part1 = Bluetooth HC-05 Macho
  Part3 = Arduino Uno (Rev3)
  Mod1 = KY-019 5V Relay Module [package="Breakout board"]
  Part4 = Logic Level Converter

nets:
  N1: Part1.TXD, Part3.D0/RX
  N2: Part1.RXD, Part4.LV
  VCC: Part1.VCC, Part3.5V, Mod1.+
  GND: Part1.GND, Part3.GND, Mod1.-, Part4.GND
  N3: Part3.D1/TX, Part4.HV
  N4: Part3.D7, Mod1.S

custom parts:
  KY-019 5V Relay Module: KY-019 5V Relay module, used to control AC circuits. (Special thanks to vanepp for fixing the PCB holes and other errors)
